# Fritzing sketch smsServer (saved by Fritzing 0.9.3b)
circuit board: 8cm x 6cm
breadboards: 1

parts:
  U1 = WeMos D1 Mini
  U4 = Arduino Nano (Rev3.0) (ICSP)
  U3 = attiny85 [package=dip]
  R1 = Resistor [tolerance=±5% resistance=470 package=THT]
  U2 = A6 mini GPS/GPRS [package="DIP (Dual Inline) [THT]"]
  C1 = Electrolytic Capacitor [capacitance=1000μF voltage=20V package="1010 [SMD, electrolytic]"]

nets:
  5V: U1.5V, U4.5V, U3.Pin_8, U2.5V, C1.+
  N1: U1.D1, U4.A5
  N2: U1.D2, U4.A4
  N3: U1.D4, U3.Pin_6
  N4: U1.D5, U2.RST
  N5: U1.D6, U4.RESET
  N6: U1.D7, U2.URX
  N7: U1.D8, U2.UTX
  GND: U1.G, U4.GND, U3.Pin_4, U2.GND, C1.-
  N8: U1.RST, R1.Pin_1
  N9: U3.Pin_5, R1.Pin_0

custom parts:
  WeMos D1 Mini: The D1 mini is a mini wifi board based on ESP-8266EX.
  A6 mini GPS/GPRS: A6 mini GPS/GPRS Module
